# Fritzing sketch ControlloStrisciaLed (saved by Fritzing 0.9.3b)
breadboards: 1

parts:
  Componente1 = Arduino Uno (Rev3)
  R1 = Resistor [tolerance=±5% resistance=370 package=THT]

nets:
  N1: Componente1.D9_PWM, R1.Pin_0

notes:
  5V power
  da esso passeranno i dati per controllare i singoli led rgb
  GND
