# Fritzing sketch ProgettazioneFritz (saved by Fritzing 0.9.3b)
breadboards: 1

parts:
  Componente1 = Arduino Uno (Rev3)
  C1 = Electrolytic Capacitor [capacitance=1000µF package="300 mil [THT, electrolytic]"]
  R2 = Resistor [tolerance=±5% resistance=220 package=THT]

nets:
  N1: Componente1.D6_PWM, R2.Pin_0
  N2: Componente1.5V, C1.+
  N3: Componente1.GND, C1.-

notes:
  Ventola
  Da esso passeranno i dati per controllare i singoli led rgb
  Alimentatore
